# Fritzing sketch THESIS_SCHEMATIC (saved by Fritzing 1.0.6)

parts:
  U1 = SHT31 Breakout (VIN GND SCL SDA AD AL)
  U2 = YYS SM4-C2H4 Ethylene Gas Sensor
  U3 = ESP32-S3-DevKitC-1 (N16R8)
  U4 = YYS SM4-C2H4 Ethylene Gas Sensor
  U5 = SHT31 Breakout (VIN GND SCL SDA AD AL)
  M2 = DC 12V Cooling Fan
  BT2 = LiFePO4 Battery 12V 12Ah
  Q2 = HW-517 Dual MOSFET Trigger Switch 5-36V 400W
  U6 = HW-688 DC-DC Buck Converter 9-36V to 5V 5A USB
  Q3 = HW-517 Dual MOSFET Trigger Switch 5-36V 400W
  M3 = DC 12V Cooling Fan
  SD2 = Micro SD (TF) Card Module, 6-pin SPI

nets:
  VIN: U1.VIN, U3.3V3, U5.VIN, SD2.3V3
  GND: U1.GND, U1.AD, U2.GND, U3.GND, U4.GND, U5.GND, U5.AD, BT2.-, Q2.GND, Q2.DC-, U6.VIN-, U6.JACK-, Q3.GND, Q3.DC-, SD2.GND
  N1: U1.SCL, U3.GPIO5
  N2: U1.SDA, U3.GPIO4
  VCC: U2.VCC, U3.5V0, U4.VCC
  N3: U2.RXD, U3.GPIO18
  N4: U2.TXD, U3.GPIO17
  N5: U3.GPIO6, Q2.PWM+
  N6: U3.GPIO7, Q3.PWM+
  N7: U3.GPIO15, U4.TXD
  N8: U3.GPIO16, U4.RXD
  N9: U3.GPIO8, U5.SDA
  N10: U3.GPIO9, U5.SCL
  N11: U3.GPIO10, SD2.CS
  N12: U3.GPIO11, SD2.MOSI
  N13: U3.GPIO12, SD2.CLK
  N14: U3.GPIO13, SD2.MISO
  N15: M2.+, BT2.+, Q2.OUT+, Q2.DC+, U6.VIN+, U6.JACK+, Q3.OUT+, Q3.DC+, M3.+
  N16: M2.-, Q2.OUT-
  N17: Q3.OUT-, M3.-

custom parts:
  SHT31 Breakout (VIN GND SCL SDA AD AL): SHT31 I2C temperature/humidity sensor breakout, 6 pads: VIN, GND, SCL, SDA (0.1in pitch column) plus AD and AL. Board approx. 0.5 x 0.6 in.
  YYS SM4-C2H4 Ethylene Gas Sensor: YYS SM4-C2H4 UART ethylene gas sensor module, 4 pins: VCC, GND, RXD, TXD. Approx. 24 mm diameter.
  ESP32-S3-DevKitC-1 (N16R8): ESP32-S3-DevKitC-1 board with ESP32-S3-WROOM-1 N16R8 module. 2 x 21 pin headers at 0.1in pitch, 0.9in row spacing; board approx. 1.0 x 2.72 in. Note: GPIO35, 36 and 37 are used by the octal PSRAM on N16R8.
  DC 12V Cooling Fan: DC 12V two-wire cooling fan (red +, black -). Drawing is a generic 80 x 80 mm fan.
  LiFePO4 Battery 12V 12Ah: 12V LiFePO4 battery pack (4S), 12Ah, F2 / faston tab terminals. Drawing is about 151 x 95 mm, the usual 12V 12Ah case size; the 24Ah version is larger.
  HW-517 Dual MOSFET Trigger Switch 5-36V 400W: HW-517 dual MOSFET trigger switch / PWM driver board. Signal 3.3-20V on PWM+/GND switches the load between OUT+ and OUT-. Power 5-36V on DC+/DC-, 15A continuous (400W). Low-side switching: OUT+ = DC+, GND = DC-. Approx. 40 x 24 mm.
  HW-688 DC-DC Buck Converter 9-36V to 5V 5A USB: HW-688 DC-DC step-down module, 9-36V in (screw terminal or 5.5x2.1mm DC jack), 5.2V 5A out (screw terminal or USB-A) with fast charge ID chip. Approx. 65 x 28 x 13 mm.
  Micro SD (TF) Card Module, 6-pin SPI: Micro SD (TF card) storage expansion board with 6-pin SPI header: 3V3, CS, MOSI, CLK, MISO, GND (2.54 mm pitch). Board approx. 20 x 20 mm.
